// Logisim project AND16.circ as structural Verilog: 1 circuit, main circuit main
module main (
  input  [15:0] in_1,
  input  [15:0] in_2,
  input  in_3,
  input  in_4,
  input  in_5,
  input  in_6,
  input  in_7,
  input  in_8,
  input  in_9,
  input  in_10,
  input  in_11,
  input  in_12,
  input  in_13,
  input  in_14,
  input  in_15,
  input  in_16,
  input  in_17,
  input  in_18,
  input  in_19,
  input  in_20,
  input  in_21,
  input  in_22,
  input  in_23,
  input  in_24,
  input  in_25,
  input  in_26,
  input  in_27,
  input  in_28,
  input  in_29,
  input  in_30,
  input  in_31,
  input  in_32,
  input  in_33,
  input  in_34,
  input  in_35,
  input  in_36,
  input  in_37,
  input  in_38,
  input  in_39,
  input  in_40,
  input  in_41,
  input  in_42,
  input  in_43,
  input  in_44,
  input  in_45,
  input  in_46,
  input  in_47,
  input  in_48,
  input  in_49,
  input  in_50,
  input  in_51,
  input  in_52,
  input  in_53,
  input  in_54,
  input  in_55,
  input  in_56,
  input  in_57,
  input  in_58,
  input  in_59,
  input  in_60,
  input  in_61,
  input  in_62,
  input  in_63,
  input  in_64,
  input  in_65,
  input  in_66,
  output [15:0] out_67,
  output [15:0] out_68,
  output [15:0] out_69
);

  wire nand_1_out, nand_2_out, nand_3_out, nand_4_out, nand_5_out, nand_6_out, nand_7_out, nand_8_out,
       nand_9_out, nand_10_out, nand_11_out, nand_12_out, nand_13_out, nand_14_out, nand_15_out, nand_16_out;

  assign out_67 = in_1 & in_2;  // AND_Gate and_1, 16 bits wide
  and and_2 (out_68[15], in_3, in_19);
  and and_3 (out_68[14], in_4, in_20);
  and and_4 (out_68[13], in_5, in_21);
  and and_5 (out_68[12], in_6, in_22);
  and and_6 (out_68[11], in_7, in_23);
  and and_7 (out_68[10], in_8, in_24);
  and and_8 (out_68[9], in_9, in_25);
  and and_9 (out_68[8], in_10, in_26);
  and and_10 (out_68[7], in_11, in_27);
  and and_11 (out_68[6], in_12, in_28);
  and and_12 (out_68[5], in_13, in_29);
  and and_13 (out_68[4], in_14, in_30);
  and and_14 (out_68[3], in_15, in_31);
  and and_15 (out_68[2], in_16, in_32);
  and and_16 (out_68[1], in_17, in_33);
  and and_17 (out_68[0], in_18, in_34);
  nand nand_1 (nand_1_out, in_35, in_51);
  nand nand_2 (nand_2_out, in_36, in_52);
  nand nand_3 (nand_3_out, in_37, in_53);
  nand nand_4 (nand_4_out, in_38, in_54);
  nand nand_5 (nand_5_out, in_39, in_55);
  nand nand_6 (nand_6_out, in_40, in_56);
  nand nand_7 (nand_7_out, in_41, in_57);
  nand nand_8 (nand_8_out, in_42, in_58);
  nand nand_9 (nand_9_out, in_43, in_59);
  nand nand_10 (nand_10_out, in_44, in_60);
  nand nand_11 (nand_11_out, in_45, in_61);
  nand nand_12 (nand_12_out, in_46, in_62);
  nand nand_13 (nand_13_out, in_47, in_63);
  nand nand_14 (nand_14_out, in_48, in_64);
  nand nand_15 (nand_15_out, in_49, in_65);
  nand nand_16 (nand_16_out, in_50, in_66);
  nand nand_17 (out_69[15], nand_1_out, nand_1_out);
  nand nand_18 (out_69[14], nand_2_out, nand_2_out);
  nand nand_19 (out_69[13], nand_3_out, nand_3_out);
  nand nand_20 (out_69[12], nand_4_out, nand_4_out);
  nand nand_21 (out_69[11], nand_5_out, nand_5_out);
  nand nand_22 (out_69[10], nand_6_out, nand_6_out);
  nand nand_23 (out_69[9], nand_7_out, nand_7_out);
  nand nand_24 (out_69[8], nand_8_out, nand_8_out);
  nand nand_25 (out_69[7], nand_9_out, nand_9_out);
  nand nand_26 (out_69[6], nand_10_out, nand_10_out);
  nand nand_27 (out_69[5], nand_11_out, nand_11_out);
  nand nand_28 (out_69[4], nand_12_out, nand_12_out);
  nand nand_29 (out_69[3], nand_13_out, nand_13_out);
  nand nand_30 (out_69[2], nand_14_out, nand_14_out);
  nand nand_31 (out_69[1], nand_15_out, nand_15_out);
  nand nand_32 (out_69[0], nand_16_out, nand_16_out);

  // Notes on the sheet:
  //   16-bit AND
  //   16-bit AND from NAND
  //   16-bit AND spread out
endmodule
