// Logisim project DMUX.circ as structural Verilog: 1 circuit, main circuit main
module main (
  input  in_1,
  input  in_2,
  output out_3,
  output out_4,
  output out_5,
  output out_6,
  output out_7,
  output out_8
);

  wire nand_1_out, nand_2_out, nand_3_out, not_1_out;

  Demultiplexer demultiplexer_1 (.out0(out_3), .out1(out_4), .in(in_1), .sel(in_2));  // open: en
  not not_1 (not_1_out, in_2);
  nand nand_1 (nand_1_out, in_2, in_2);
  and and_1 (out_5, in_1, not_1_out);
  and and_2 (out_6, in_2, in_1);
  nand nand_2 (nand_2_out, in_1, nand_1_out);
  nand nand_3 (nand_3_out, in_2, in_1);
  nand nand_4 (out_7, nand_2_out, nand_2_out);
  nand nand_5 (out_8, nand_3_out, nand_3_out);

  // Notes on the sheet:
  //   DMUX
  //   DMUX from previous gates
  //   DMUX from NAND only
endmodule
