// Logisim project MUX.circ as structural Verilog: 1 circuit, main circuit main
module main (
  input  B,
  input  sel,
  input  A,
  output out_4,
  output out_5,
  output out_6
);

  wire and_1_out, and_2_out, nand_1_out, nand_2_out, nand_3_out, nand_4_out, nand_5_out, nand_6_out,
       nand_7_out, nand_8_out, nand_9_out, nand_10_out, not_1_out;

  nand nand_1 (nand_1_out, sel, sel);
  nand nand_2 (nand_2_out, B, sel);
  nand nand_3 (nand_3_out, nand_1_out, A);
  nand nand_4 (nand_4_out, nand_2_out, nand_2_out);
  nand nand_5 (nand_5_out, nand_3_out, nand_3_out);
  Multiplexer multiplexer_1 (.in0(A), .in1(B), .out(out_4), .sel(sel));  // open: en
  not not_1 (not_1_out, sel);
  nand nand_6 (nand_6_out, nand_4_out, nand_5_out);
  nand nand_7 (nand_7_out, nand_5_out, nand_5_out);
  nand nand_8 (nand_8_out, nand_4_out, nand_4_out);
  and and_1 (and_1_out, B, sel);
  and and_2 (and_2_out, not_1_out, A);
  nand nand_9 (nand_9_out, nand_7_out, nand_8_out);
  nand nand_10 (nand_10_out, nand_6_out, nand_9_out);
  xor xor_1 (out_5, and_1_out, and_2_out);
  nand nand_11 (out_6, nand_10_out, nand_10_out);

  // Notes on the sheet:
  //   NOT
  //   AND
  //   AND
  //   MUX from NAND only
  //   MUX
  //   OR
  //   MUX from previous gates
  //   XOR
  //   AND
endmodule
