// Logisim project MUX16.circ as structural Verilog: 1 circuit, main circuit main
module main (
  input  [15:0] in_1,
  input  [15:0] in_2,
  input  in_3,
  input  in_4,
  input  in_5,
  input  in_6,
  input  in_7,
  input  in_8,
  input  in_9,
  input  in_10,
  input  in_11,
  input  in_12,
  input  in_13,
  input  in_14,
  input  in_15,
  input  in_16,
  input  in_17,
  input  in_18,
  input  in_19,
  input  SEL,
  input  in_21,
  input  in_22,
  input  in_23,
  input  in_24,
  input  in_25,
  input  in_26,
  input  in_27,
  input  in_28,
  input  in_29,
  input  in_30,
  input  in_31,
  input  in_32,
  input  in_33,
  input  in_34,
  input  in_35,
  input  in_36,
  output [15:0] out_37,
  output [15:0] out_38
);

  wire nand_1_out, nand_2_out, nand_3_out, nand_4_out, nand_5_out, nand_6_out, nand_7_out, nand_8_out,
       nand_9_out, nand_10_out, nand_11_out, nand_12_out, nand_13_out, nand_14_out, nand_15_out, nand_16_out,
       nand_17_out, nand_18_out, nand_19_out, nand_20_out, nand_21_out, nand_22_out, nand_23_out,
       nand_24_out, nand_25_out, nand_26_out, nand_27_out, nand_28_out, nand_29_out, nand_30_out,
       nand_31_out, nand_32_out, nand_33_out, nand_34_out, nand_35_out, nand_36_out, nand_37_out,
       nand_38_out, nand_39_out, nand_40_out, nand_41_out, nand_42_out, nand_43_out, nand_44_out,
       nand_45_out, nand_46_out, nand_47_out, nand_48_out, nand_49_out, nand_50_out, nand_51_out,
       nand_52_out, nand_53_out, nand_54_out, nand_55_out, nand_56_out, nand_57_out, nand_58_out,
       nand_59_out, nand_60_out, nand_61_out, nand_62_out, nand_63_out, nand_64_out, nand_65_out,
       nand_66_out, nand_67_out, nand_68_out, nand_69_out, nand_70_out, nand_71_out, nand_72_out,
       nand_73_out, nand_74_out, nand_75_out, nand_76_out, nand_77_out, nand_78_out, nand_79_out,
       nand_80_out, nand_81_out, nand_82_out, nand_83_out, nand_84_out, nand_85_out, nand_86_out,
       nand_87_out, nand_88_out, nand_89_out, nand_90_out, nand_91_out, nand_92_out, nand_93_out,
       nand_94_out, nand_95_out, nand_96_out, nand_97_out, nand_98_out, nand_99_out, nand_100_out,
       nand_101_out, nand_102_out, nand_103_out, nand_104_out, nand_105_out, nand_106_out, nand_107_out,
       nand_108_out, nand_109_out, nand_110_out, nand_111_out, nand_112_out, nand_113_out, nand_114_out,
       nand_115_out, nand_116_out, nand_117_out, nand_118_out, nand_119_out, nand_120_out, nand_121_out,
       nand_122_out, nand_123_out, nand_124_out, nand_125_out, nand_126_out, nand_127_out, nand_128_out,
       nand_129_out, nand_130_out, nand_131_out, nand_132_out, nand_133_out, nand_134_out, nand_135_out,
       nand_136_out, nand_137_out, nand_138_out, nand_139_out, nand_140_out, nand_141_out, nand_142_out,
       nand_143_out, nand_144_out, nand_145_out, nand_146_out, nand_147_out, nand_148_out, nand_149_out,
       nand_150_out, nand_151_out, nand_152_out, nand_153_out, nand_154_out, nand_155_out, nand_156_out,
       nand_157_out, nand_158_out, nand_159_out, nand_160_out;

  Multiplexer #(.width(16)) multiplexer_1 (.in0(in_1), .in1(in_2), .out(out_37), .sel(in_3));  // open: en
  nand nand_1 (nand_1_out, SEL, SEL);
  nand nand_2 (nand_2_out, SEL, SEL);
  nand nand_3 (nand_3_out, SEL, SEL);
  nand nand_4 (nand_4_out, SEL, SEL);
  nand nand_5 (nand_5_out, SEL, SEL);
  nand nand_6 (nand_6_out, SEL, SEL);
  nand nand_7 (nand_7_out, SEL, SEL);
  nand nand_8 (nand_8_out, SEL, SEL);
  nand nand_9 (nand_9_out, SEL, SEL);
  nand nand_10 (nand_10_out, SEL, SEL);
  nand nand_11 (nand_11_out, SEL, SEL);
  nand nand_12 (nand_12_out, SEL, SEL);
  nand nand_13 (nand_13_out, SEL, SEL);
  nand nand_14 (nand_14_out, SEL, SEL);
  nand nand_15 (nand_15_out, SEL, SEL);
  nand nand_16 (nand_16_out, SEL, SEL);
  nand nand_17 (nand_17_out, in_12, SEL);
  nand nand_18 (nand_18_out, nand_1_out, in_4);
  nand nand_19 (nand_19_out, in_13, SEL);
  nand nand_20 (nand_20_out, nand_2_out, in_5);
  nand nand_21 (nand_21_out, in_14, SEL);
  nand nand_22 (nand_22_out, nand_3_out, in_6);
  nand nand_23 (nand_23_out, in_15, SEL);
  nand nand_24 (nand_24_out, nand_4_out, in_7);
  nand nand_25 (nand_25_out, in_16, SEL);
  nand nand_26 (nand_26_out, nand_5_out, in_8);
  nand nand_27 (nand_27_out, in_17, SEL);
  nand nand_28 (nand_28_out, nand_6_out, in_9);
  nand nand_29 (nand_29_out, in_18, SEL);
  nand nand_30 (nand_30_out, nand_7_out, in_10);
  nand nand_31 (nand_31_out, in_19, SEL);
  nand nand_32 (nand_32_out, nand_8_out, in_11);
  nand nand_33 (nand_33_out, in_29, SEL);
  nand nand_34 (nand_34_out, nand_9_out, in_21);
  nand nand_35 (nand_35_out, in_30, SEL);
  nand nand_36 (nand_36_out, nand_10_out, in_22);
  nand nand_37 (nand_37_out, in_31, SEL);
  nand nand_38 (nand_38_out, nand_11_out, in_23);
  nand nand_39 (nand_39_out, in_32, SEL);
  nand nand_40 (nand_40_out, nand_12_out, in_24);
  nand nand_41 (nand_41_out, in_33, SEL);
  nand nand_42 (nand_42_out, nand_13_out, in_25);
  nand nand_43 (nand_43_out, in_34, SEL);
  nand nand_44 (nand_44_out, nand_14_out, in_26);
  nand nand_45 (nand_45_out, in_35, SEL);
  nand nand_46 (nand_46_out, nand_15_out, in_27);
  nand nand_47 (nand_47_out, in_36, SEL);
  nand nand_48 (nand_48_out, nand_16_out, in_28);
  nand nand_49 (nand_49_out, nand_17_out, nand_17_out);
  nand nand_50 (nand_50_out, nand_18_out, nand_18_out);
  nand nand_51 (nand_51_out, nand_19_out, nand_19_out);
  nand nand_52 (nand_52_out, nand_20_out, nand_20_out);
  nand nand_53 (nand_53_out, nand_21_out, nand_21_out);
  nand nand_54 (nand_54_out, nand_22_out, nand_22_out);
  nand nand_55 (nand_55_out, nand_23_out, nand_23_out);
  nand nand_56 (nand_56_out, nand_24_out, nand_24_out);
  nand nand_57 (nand_57_out, nand_25_out, nand_25_out);
  nand nand_58 (nand_58_out, nand_26_out, nand_26_out);
  nand nand_59 (nand_59_out, nand_27_out, nand_27_out);
  nand nand_60 (nand_60_out, nand_28_out, nand_28_out);
  nand nand_61 (nand_61_out, nand_29_out, nand_29_out);
  nand nand_62 (nand_62_out, nand_30_out, nand_30_out);
  nand nand_63 (nand_63_out, nand_31_out, nand_31_out);
  nand nand_64 (nand_64_out, nand_32_out, nand_32_out);
  nand nand_65 (nand_65_out, nand_33_out, nand_33_out);
  nand nand_66 (nand_66_out, nand_34_out, nand_34_out);
  nand nand_67 (nand_67_out, nand_35_out, nand_35_out);
  nand nand_68 (nand_68_out, nand_36_out, nand_36_out);
  nand nand_69 (nand_69_out, nand_37_out, nand_37_out);
  nand nand_70 (nand_70_out, nand_38_out, nand_38_out);
  nand nand_71 (nand_71_out, nand_39_out, nand_39_out);
  nand nand_72 (nand_72_out, nand_40_out, nand_40_out);
  nand nand_73 (nand_73_out, nand_41_out, nand_41_out);
  nand nand_74 (nand_74_out, nand_42_out, nand_42_out);
  nand nand_75 (nand_75_out, nand_43_out, nand_43_out);
  nand nand_76 (nand_76_out, nand_44_out, nand_44_out);
  nand nand_77 (nand_77_out, nand_45_out, nand_45_out);
  nand nand_78 (nand_78_out, nand_46_out, nand_46_out);
  nand nand_79 (nand_79_out, nand_47_out, nand_47_out);
  nand nand_80 (nand_80_out, nand_48_out, nand_48_out);
  nand nand_81 (nand_81_out, nand_49_out, nand_50_out);
  nand nand_82 (nand_82_out, nand_50_out, nand_50_out);
  nand nand_83 (nand_83_out, nand_49_out, nand_49_out);
  nand nand_84 (nand_84_out, nand_51_out, nand_52_out);
  nand nand_85 (nand_85_out, nand_52_out, nand_52_out);
  nand nand_86 (nand_86_out, nand_51_out, nand_51_out);
  nand nand_87 (nand_87_out, nand_53_out, nand_54_out);
  nand nand_88 (nand_88_out, nand_54_out, nand_54_out);
  nand nand_89 (nand_89_out, nand_53_out, nand_53_out);
  nand nand_90 (nand_90_out, nand_55_out, nand_56_out);
  nand nand_91 (nand_91_out, nand_56_out, nand_56_out);
  nand nand_92 (nand_92_out, nand_55_out, nand_55_out);
  nand nand_93 (nand_93_out, nand_57_out, nand_58_out);
  nand nand_94 (nand_94_out, nand_58_out, nand_58_out);
  nand nand_95 (nand_95_out, nand_57_out, nand_57_out);
  nand nand_96 (nand_96_out, nand_59_out, nand_60_out);
  nand nand_97 (nand_97_out, nand_60_out, nand_60_out);
  nand nand_98 (nand_98_out, nand_59_out, nand_59_out);
  nand nand_99 (nand_99_out, nand_61_out, nand_62_out);
  nand nand_100 (nand_100_out, nand_62_out, nand_62_out);
  nand nand_101 (nand_101_out, nand_61_out, nand_61_out);
  nand nand_102 (nand_102_out, nand_63_out, nand_64_out);
  nand nand_103 (nand_103_out, nand_64_out, nand_64_out);
  nand nand_104 (nand_104_out, nand_63_out, nand_63_out);
  nand nand_105 (nand_105_out, nand_65_out, nand_66_out);
  nand nand_106 (nand_106_out, nand_66_out, nand_66_out);
  nand nand_107 (nand_107_out, nand_65_out, nand_65_out);
  nand nand_108 (nand_108_out, nand_67_out, nand_68_out);
  nand nand_109 (nand_109_out, nand_68_out, nand_68_out);
  nand nand_110 (nand_110_out, nand_67_out, nand_67_out);
  nand nand_111 (nand_111_out, nand_69_out, nand_70_out);
  nand nand_112 (nand_112_out, nand_70_out, nand_70_out);
  nand nand_113 (nand_113_out, nand_69_out, nand_69_out);
  nand nand_114 (nand_114_out, nand_71_out, nand_72_out);
  nand nand_115 (nand_115_out, nand_72_out, nand_72_out);
  nand nand_116 (nand_116_out, nand_71_out, nand_71_out);
  nand nand_117 (nand_117_out, nand_73_out, nand_74_out);
  nand nand_118 (nand_118_out, nand_74_out, nand_74_out);
  nand nand_119 (nand_119_out, nand_73_out, nand_73_out);
  nand nand_120 (nand_120_out, nand_75_out, nand_76_out);
  nand nand_121 (nand_121_out, nand_76_out, nand_76_out);
  nand nand_122 (nand_122_out, nand_75_out, nand_75_out);
  nand nand_123 (nand_123_out, nand_77_out, nand_78_out);
  nand nand_124 (nand_124_out, nand_78_out, nand_78_out);
  nand nand_125 (nand_125_out, nand_77_out, nand_77_out);
  nand nand_126 (nand_126_out, nand_79_out, nand_80_out);
  nand nand_127 (nand_127_out, nand_80_out, nand_80_out);
  nand nand_128 (nand_128_out, nand_79_out, nand_79_out);
  nand nand_129 (nand_129_out, nand_82_out, nand_83_out);
  nand nand_130 (nand_130_out, nand_85_out, nand_86_out);
  nand nand_131 (nand_131_out, nand_88_out, nand_89_out);
  nand nand_132 (nand_132_out, nand_91_out, nand_92_out);
  nand nand_133 (nand_133_out, nand_94_out, nand_95_out);
  nand nand_134 (nand_134_out, nand_97_out, nand_98_out);
  nand nand_135 (nand_135_out, nand_100_out, nand_101_out);
  nand nand_136 (nand_136_out, nand_103_out, nand_104_out);
  nand nand_137 (nand_137_out, nand_106_out, nand_107_out);
  nand nand_138 (nand_138_out, nand_109_out, nand_110_out);
  nand nand_139 (nand_139_out, nand_112_out, nand_113_out);
  nand nand_140 (nand_140_out, nand_115_out, nand_116_out);
  nand nand_141 (nand_141_out, nand_118_out, nand_119_out);
  nand nand_142 (nand_142_out, nand_121_out, nand_122_out);
  nand nand_143 (nand_143_out, nand_124_out, nand_125_out);
  nand nand_144 (nand_144_out, nand_127_out, nand_128_out);
  nand nand_145 (nand_145_out, nand_81_out, nand_129_out);
  nand nand_146 (nand_146_out, nand_84_out, nand_130_out);
  nand nand_147 (nand_147_out, nand_87_out, nand_131_out);
  nand nand_148 (nand_148_out, nand_90_out, nand_132_out);
  nand nand_149 (nand_149_out, nand_93_out, nand_133_out);
  nand nand_150 (nand_150_out, nand_96_out, nand_134_out);
  nand nand_151 (nand_151_out, nand_99_out, nand_135_out);
  nand nand_152 (nand_152_out, nand_102_out, nand_136_out);
  nand nand_153 (nand_153_out, nand_105_out, nand_137_out);
  nand nand_154 (nand_154_out, nand_108_out, nand_138_out);
  nand nand_155 (nand_155_out, nand_111_out, nand_139_out);
  nand nand_156 (nand_156_out, nand_114_out, nand_140_out);
  nand nand_157 (nand_157_out, nand_117_out, nand_141_out);
  nand nand_158 (nand_158_out, nand_120_out, nand_142_out);
  nand nand_159 (nand_159_out, nand_123_out, nand_143_out);
  nand nand_160 (nand_160_out, nand_126_out, nand_144_out);
  nand nand_161 (out_38[15], nand_145_out, nand_145_out);
  nand nand_162 (out_38[14], nand_146_out, nand_146_out);
  nand nand_163 (out_38[13], nand_147_out, nand_147_out);
  nand nand_164 (out_38[12], nand_148_out, nand_148_out);
  nand nand_165 (out_38[11], nand_149_out, nand_149_out);
  nand nand_166 (out_38[10], nand_150_out, nand_150_out);
  nand nand_167 (out_38[9], nand_151_out, nand_151_out);
  nand nand_168 (out_38[8], nand_152_out, nand_152_out);
  nand nand_169 (out_38[7], nand_153_out, nand_153_out);
  nand nand_170 (out_38[6], nand_154_out, nand_154_out);
  nand nand_171 (out_38[5], nand_155_out, nand_155_out);
  nand nand_172 (out_38[4], nand_156_out, nand_156_out);
  nand nand_173 (out_38[3], nand_157_out, nand_157_out);
  nand nand_174 (out_38[2], nand_158_out, nand_158_out);
  nand nand_175 (out_38[1], nand_159_out, nand_159_out);
  nand nand_176 (out_38[0], nand_160_out, nand_160_out);

  // Notes on the sheet:
  //   A
  //   B
endmodule
