// Logisim project NOT.circ as structural Verilog: 1 circuit, main circuit main
module main (
  input  in_1,
  output out_2,
  output out_3
);

  nand nand_1 (out_2, in_1, in_1);
  not not_1 (out_3, in_1);

  // Notes on the sheet:
  //   NAND implementation of a NOT gate
  //   NOT gate
endmodule
