// Logisim project NOT16.circ as structural Verilog: 1 circuit, main circuit main
module main (
  input  [15:0] in_1,
  input  in_2,
  input  in_3,
  input  in_4,
  input  in_5,
  input  in_6,
  input  in_7,
  input  in_8,
  input  in_9,
  input  in_10,
  input  in_11,
  input  in_12,
  input  in_13,
  input  in_14,
  input  in_15,
  input  in_16,
  input  in_17,
  output [15:0] out_18,
  output [15:0] out_19,
  output [15:0] out_20
);

  assign out_18 = ~in_1;  // NOT_Gate not_1, 16 bits wide
  not not_2 (out_19[15], in_2);
  not not_3 (out_19[14], in_3);
  not not_4 (out_19[13], in_4);
  not not_5 (out_19[12], in_5);
  not not_6 (out_19[11], in_6);
  not not_7 (out_19[10], in_7);
  not not_8 (out_19[9], in_8);
  not not_9 (out_19[8], in_9);
  not not_10 (out_19[7], in_10);
  not not_11 (out_19[6], in_11);
  not not_12 (out_19[5], in_12);
  not not_13 (out_19[4], in_13);
  not not_14 (out_19[3], in_14);
  not not_15 (out_19[2], in_15);
  not not_16 (out_19[1], in_16);
  not not_17 (out_19[0], in_17);
  nand nand_1 (out_20[15], in_2, in_2);
  nand nand_2 (out_20[14], in_3, in_3);
  nand nand_3 (out_20[13], in_4, in_4);
  nand nand_4 (out_20[12], in_5, in_5);
  nand nand_5 (out_20[11], in_6, in_6);
  nand nand_6 (out_20[10], in_7, in_7);
  nand nand_7 (out_20[9], in_8, in_8);
  nand nand_8 (out_20[8], in_9, in_9);
  nand nand_9 (out_20[7], in_10, in_10);
  nand nand_10 (out_20[6], in_11, in_11);
  nand nand_11 (out_20[5], in_12, in_12);
  nand nand_12 (out_20[4], in_13, in_13);
  nand nand_13 (out_20[3], in_14, in_14);
  nand nand_14 (out_20[2], in_15, in_15);
  nand nand_15 (out_20[1], in_16, in_16);
  nand nand_16 (out_20[0], in_17, in_17);

  // Notes on the sheet:
  //   16-bit NOT
  //   16-bit NOT spread out
  //   16-bit NOT from NAND
endmodule
