// Logisim project OR.circ as structural Verilog: 1 circuit, main circuit main
module main (
  input  in_1,
  input  in_2,
  output out_3,
  output out_4,
  output out_5
);

  wire nand_1_out, nand_2_out, not_1_out, not_2_out;

  nand nand_1 (nand_1_out, in_1, in_1);
  nand nand_2 (nand_2_out, in_2, in_2);
  not not_1 (not_1_out, in_1);
  not not_2 (not_2_out, in_2);
  or or_1 (out_5, in_1, in_2);
  nand nand_3 (out_4, not_1_out, not_2_out);
  nand nand_4 (out_3, nand_1_out, nand_2_out);

  // Notes on the sheet:
  //   OR from NAND only
  //   OR from previous gates
  //   OR
endmodule
