// Logisim project OR16.circ as structural Verilog: 1 circuit, main circuit main
module main (
  input  [15:0] in_1,
  input  [15:0] in_2,
  input  in_3,
  input  in_4,
  input  in_5,
  input  in_6,
  input  in_7,
  input  in_8,
  input  in_9,
  input  in_10,
  input  in_11,
  input  in_12,
  input  in_13,
  input  in_14,
  input  in_15,
  input  in_16,
  input  in_17,
  input  in_18,
  input  in_19,
  input  in_20,
  input  in_21,
  input  in_22,
  input  in_23,
  input  in_24,
  input  in_25,
  input  in_26,
  input  in_27,
  input  in_28,
  input  in_29,
  input  in_30,
  input  in_31,
  input  in_32,
  input  in_33,
  input  in_34,
  output [15:0] out_35,
  output [15:0] out_36
);

  wire nand_1_out, nand_2_out, nand_3_out, nand_4_out, nand_5_out, nand_6_out, nand_7_out, nand_8_out,
       nand_9_out, nand_10_out, nand_11_out, nand_12_out, nand_13_out, nand_14_out, nand_15_out, nand_16_out,
       nand_17_out, nand_18_out, nand_19_out, nand_20_out, nand_21_out, nand_22_out, nand_23_out,
       nand_24_out, nand_25_out, nand_26_out, nand_27_out, nand_28_out, nand_29_out, nand_30_out,
       nand_31_out, nand_32_out;

  assign out_35 = in_1 | in_2;  // OR_Gate or_1, 16 bits wide
  nand nand_1 (nand_1_out, in_3, in_3);
  nand nand_2 (nand_2_out, in_19, in_19);
  nand nand_3 (nand_3_out, in_4, in_4);
  nand nand_4 (nand_4_out, in_20, in_20);
  nand nand_5 (nand_5_out, in_5, in_5);
  nand nand_6 (nand_6_out, in_21, in_21);
  nand nand_7 (nand_7_out, in_6, in_6);
  nand nand_8 (nand_8_out, in_22, in_22);
  nand nand_9 (nand_9_out, in_7, in_7);
  nand nand_10 (nand_10_out, in_23, in_23);
  nand nand_11 (nand_11_out, in_8, in_8);
  nand nand_12 (nand_12_out, in_24, in_24);
  nand nand_13 (nand_13_out, in_9, in_9);
  nand nand_14 (nand_14_out, in_25, in_25);
  nand nand_15 (nand_15_out, in_10, in_10);
  nand nand_16 (nand_16_out, in_26, in_26);
  nand nand_17 (nand_17_out, in_11, in_11);
  nand nand_18 (nand_18_out, in_27, in_27);
  nand nand_19 (nand_19_out, in_12, in_12);
  nand nand_20 (nand_20_out, in_28, in_28);
  nand nand_21 (nand_21_out, in_13, in_13);
  nand nand_22 (nand_22_out, in_29, in_29);
  nand nand_23 (nand_23_out, in_14, in_14);
  nand nand_24 (nand_24_out, in_30, in_30);
  nand nand_25 (nand_25_out, in_15, in_15);
  nand nand_26 (nand_26_out, in_31, in_31);
  nand nand_27 (nand_27_out, in_16, in_16);
  nand nand_28 (nand_28_out, in_32, in_32);
  nand nand_29 (nand_29_out, in_17, in_17);
  nand nand_30 (nand_30_out, in_33, in_33);
  nand nand_31 (nand_31_out, in_18, in_18);
  nand nand_32 (nand_32_out, in_34, in_34);
  nand nand_33 (out_36[15], nand_1_out, nand_2_out);
  nand nand_34 (out_36[14], nand_3_out, nand_4_out);
  nand nand_35 (out_36[13], nand_5_out, nand_6_out);
  nand nand_36 (out_36[12], nand_7_out, nand_8_out);
  nand nand_37 (out_36[11], nand_9_out, nand_10_out);
  nand nand_38 (out_36[10], nand_11_out, nand_12_out);
  nand nand_39 (out_36[9], nand_13_out, nand_14_out);
  nand nand_40 (out_36[8], nand_15_out, nand_16_out);
  nand nand_41 (out_36[7], nand_17_out, nand_18_out);
  nand nand_42 (out_36[6], nand_19_out, nand_20_out);
  nand nand_43 (out_36[5], nand_21_out, nand_22_out);
  nand nand_44 (out_36[4], nand_23_out, nand_24_out);
  nand nand_45 (out_36[3], nand_25_out, nand_26_out);
  nand nand_46 (out_36[2], nand_27_out, nand_28_out);
  nand nand_47 (out_36[1], nand_29_out, nand_30_out);
  nand nand_48 (out_36[0], nand_31_out, nand_32_out);
endmodule
