// Logisim project XOR.circ as structural Verilog: 1 circuit, main circuit main
module main (
  input  in_1,
  input  in_2,
  output out_3,
  output out_4,
  output out_5
);

  wire nand_1_out, nand_2_out, nand_3_out, nand_4_out, nand_5_out, nand_6_out, or_1_out;

  nand nand_1 (nand_1_out, in_1, in_2);
  nand nand_2 (nand_2_out, in_2, in_2);
  nand nand_3 (nand_3_out, in_1, in_1);
  nand nand_4 (nand_4_out, in_1, in_2);
  or or_1 (or_1_out, in_1, in_2);
  xor xor_1 (out_5, in_1, in_2);
  nand nand_5 (nand_5_out, nand_2_out, nand_3_out);
  and and_1 (out_4, nand_4_out, or_1_out);
  nand nand_6 (nand_6_out, nand_1_out, nand_5_out);
  nand nand_7 (out_3, nand_6_out, nand_6_out);

  // Notes on the sheet:
  //   OR
  //   XOR from previous gates
  //   XOR
  //   XOR form NAND only
  //   NAND
  //   AND
  //   NOT
endmodule
